# Fritzing sketch YAPMC_D1mini (saved by Fritzing 0.9.3b)
circuit board: 6.5cm x 4.75cm
breadboards: 1

parts:
  WeMos_D1_Mini1 = WeMos D1 Mini
  Hours_Meter = 7-Segment Panel Ammeter
  Mins_Meter = 7-Segment Panel Ammeter
  AM/PM_LED = LED - 5mm [color="Yellow (595nm)" package="5 mm [THT]"]
  Secs_LED = LED - 5mm [color="Yellow (595nm)" package="5 mm [THT]"]
  R1 = Resistor [tolerance=±5% resistance=220 package=THT]
  R2 = Resistor [tolerance=±5% resistance=220 package=THT]
  R3 = Resistor [tolerance=±5% resistance=220 package=THT]
  9V_Btry = Battery block 9V
  LM7805 = Voltage Regulator - 5V [package="TO220 [THT]"]
  Hours_Btn = Pushbutton [package="[SMD]"]
  Mins_Btn = Pushbutton [package="[SMD]"]
  5V_G = Screw terminal - 2 pins [package=THT]
  J4 = Screw terminal - 2 pins [package=THT]
  J5 = Screw terminal - 2 pins [package=THT]
  J6 = Screw terminal - 2 pins [package=THT]
  J7 = Screw terminal - 2 pins [package=THT]
  J8 = Screw terminal - 2 pins [package=THT]
  J9 = Screw terminal - 2 pins [package=THT]
  J11 = Screw terminal - 2 pins [package=THT]
  J12 = Screw terminal - 2 pins [package=THT]
  R4 = Resistor [tolerance=±5% resistance=220 package=THT]
  YAPMC = DIODE-ZENER [package=diode-zener]
  xCrunchy = DIODE-ZENER [package=diode-zener]

nets:
  N1: WeMos_D1_Mini1.5V, Hours_Meter.V+, Mins_Meter.V+, LM7805.output_voltage, 5V_G.pin1
  N2: WeMos_D1_Mini1.A0, J12.pin1
  N3: WeMos_D1_Mini1.D0, R2.Pin_1
  N4: WeMos_D1_Mini1.D1, Mins_Meter.LOAD-
  N5: WeMos_D1_Mini1.D2, Hours_Meter.LOAD-
  N6: WeMos_D1_Mini1.D3, J4.pin1
  N7: WeMos_D1_Mini1.D4, J5.pin1
  N8: WeMos_D1_Mini1.D5, Hours_Btn.Pin_3, Hours_Btn.Pin_4, J7.pin1
  N9: WeMos_D1_Mini1.D6, Mins_Btn.Pin_3, Mins_Btn.Pin_4, J8.pin1
  N10: WeMos_D1_Mini1.D7, R1.Pin_1
  N11: WeMos_D1_Mini1.D8, J11.pin1
  N12: WeMos_D1_Mini1.G, Hours_Meter.GND#2, Mins_Meter.GND#2, AM/PM_LED.cathode, Secs_LED.cathode, R3.Pin_1, 9V_Btry.-, LM7805.GND, Hours_Btn.Pin_1, Hours_Btn.Pin_2, Mins_Btn.Pin_1, Mins_Btn.Pin_2, J11.pin2, J12.pin2, R4.Pin_1
  N13: Hours_Meter.GND#4, R4.Pin_0
  N14: Mins_Meter.GND#4, R3.Pin_0
  N15: AM/PM_LED.anode, R2.Pin_0, J6.pin1
  N16: Secs_LED.anode, R1.Pin_0, J9.pin1
  N17: 9V_Btry.+, LM7805.input_voltage
  N18: 5V_G.pin2, J4.pin2, J5.pin2, J6.pin2, J7.pin2, J8.pin2
  N19: YAPMC.C, YAPMC.A, xCrunchy.C, xCrunchy.A

custom parts:
  7-Segment Panel Ammeter: 7-Segment Panel Ammeter (0 to 9.99A)
